// Logisim project CPU_Control.circ as structural Verilog: 13 circuits, main circuit Control
module Control (
  input  [3:0] in_1,
  output Mem_Read,
  output Mem_to_Reg,
  output Mem_Write,
  output Clock_Stop,
  output Write_ra,
  output Read_ra,
  output Reg_Write,
  output Branch,
  output ALU_op1,
  output ALU_op2,
  output ALU_Src
);

  MemRead memread_1 (.in_1(in_1), .out_2(Mem_Read));
  MemtoReg memtoreg_1 (.in_1(in_1), .out_2(Mem_to_Reg));
  MemWrite memwrite_1 (.in_1(in_1), .out_2(Mem_Write));
  Clock_Stop_8053a739 clock_stop_8053a739_1 (.in_1(in_1), .out_2(Clock_Stop));
  Write_ra_f61e1106 write_ra_f61e1106_1 (.in_1(in_1), .out_2(Write_ra));
  Read_ra_849e8755 read_ra_849e8755_1 (.in_1(in_1), .out_2(Read_ra));
  RegWrite regwrite_1 (.in_1(in_1), .out_2(Reg_Write));
  B_ranch b_ranch_1 (.in_1(in_1), .out_2(Branch));
  ALUop1 aluop1_1 (.in_1(in_1), .out_2(ALU_op1));
  ALUop2 aluop2_1 (.in_1(in_1), .out_2(ALU_op2));
  ALUSrc alusrc_1 (.in_1(in_1), .out_2(ALU_Src));
endmodule

module MemRead (
  input  [3:0] in_1,
  output out_2
);

  wire not_1_out, not_2_out, not_3_out;

  not not_1 (not_1_out, in_1[1]);
  not not_2 (not_2_out, in_1[2]);
  not not_3 (not_3_out, in_1[3]);
  and and_1 (out_2, in_1[0], not_1_out, not_2_out, not_3_out);
endmodule

module MemtoReg (
  input  [3:0] in_1,
  output out_2
);

  wire not_1_out, not_2_out, not_3_out;

  not not_1 (not_1_out, in_1[1]);
  not not_2 (not_2_out, in_1[2]);
  not not_3 (not_3_out, in_1[3]);
  and and_1 (out_2, in_1[0], not_1_out, not_2_out, not_3_out);
endmodule

module MemWrite (
  input  [3:0] in_1,
  output out_2
);

  wire not_1_out, not_2_out;

  not not_1 (not_1_out, in_1[1]);
  not not_2 (not_2_out, in_1[3]);
  and and_1 (out_2, in_1[0], not_1_out, in_1[2], not_2_out);
endmodule

module Clock_Stop_8053a739 (
  input  [3:0] in_1,
  output out_2
);

  and and_1 (out_2, in_1[0], in_1[1], in_1[2], in_1[3]);
endmodule

module Write_ra_f61e1106 (
  input  [3:0] in_1,
  output out_2
);

  wire not_1_out;

  not not_1 (not_1_out, in_1[1]);
  and and_1 (out_2, in_1[0], not_1_out, in_1[2], in_1[3]);
endmodule

module Read_ra_849e8755 (
  input  [3:0] in_1,
  output out_2
);

  wire not_1_out;

  not not_1 (not_1_out, in_1[0]);
  and and_1 (out_2, not_1_out, in_1[1], in_1[2], in_1[3]);
endmodule

module RegWrite (
  input  [3:0] in_1,
  output out_2
);

  wire and_1_out, and_2_out, and_3_out, and_4_out;

  and and_1 (and_1_out, ~in_1[0], ~in_1[1], ~in_1[3]);  // AND_Gate
  and and_2 (and_2_out, ~in_1[3], ~in_1[2], ~in_1[1]);  // AND_Gate
  and and_3 (and_3_out, in_1[3], ~in_1[2], ~in_1[1]);  // AND_Gate
  and and_4 (and_4_out, in_1[1], ~in_1[3]);  // AND_Gate
  or or_1 (out_2, and_1_out, and_2_out, and_3_out, and_4_out);
endmodule

module B_ranch (
  input  [3:0] in_1,
  output out_2
);

  wire and_1_out, and_2_out, and_3_out, and_4_out;

  and and_1 (and_1_out, in_1[2], ~in_1[1], ~in_1[0]);  // AND_Gate
  and and_2 (and_2_out, ~in_1[1], in_1[2], in_1[3]);  // AND_Gate
  and and_3 (and_3_out, in_1[1], ~in_1[2], in_1[3]);  // AND_Gate
  and and_4 (and_4_out, ~in_1[0], in_1[1], in_1[3]);  // AND_Gate
  or or_1 (out_2, and_1_out, and_2_out, and_3_out, and_4_out);
endmodule

module ALUop1 (
  input  [3:0] in_1,
  output out_2
);

  wire and_1_out, and_2_out;

  and and_1 (and_1_out, ~in_1[0], ~in_1[1], ~in_1[2], in_1[3]);  // AND_Gate
  and and_2 (and_2_out, in_1[1], ~in_1[2], in_1[3]);  // AND_Gate
  or or_1 (out_2, and_1_out, and_2_out);
endmodule

module ALUop2 (
  input  [3:0] in_1,
  output out_2
);

  wire and_1_out, and_2_out, and_3_out;

  and and_1 (and_1_out, ~in_1[1], ~in_1[2], in_1[3]);  // AND_Gate
  and and_2 (and_2_out, ~in_1[1], ~in_1[2], ~in_1[3], in_1[0]);  // AND_Gate
  and and_3 (and_3_out, in_1[1], ~in_1[2], ~in_1[3]);  // AND_Gate
  or or_1 (out_2, and_1_out, and_2_out, and_3_out);
endmodule

module ALUSrc (
  input  [3:0] in_1,
  output out_2
);

  wire and_1_out, and_2_out, and_3_out;

  and and_1 (and_1_out, ~in_1[0], ~in_1[1], ~in_1[3]);  // AND_Gate
  and and_2 (and_2_out, in_1[3], ~in_1[2], ~in_1[1]);  // AND_Gate
  and and_3 (and_3_out, in_1[0], in_1[2], ~in_1[3]);  // AND_Gate
  or or_1 (out_2, and_1_out, and_2_out, and_3_out);
endmodule

module test (
);

  Control control_1 ();  // open: in_1, Mem_Read, Mem_to_Reg, Mem_Write, Clock_Stop, Write_ra, Read_ra, Reg_Write, Branch, ALU_op1, ALU_op2, ALU_Src
endmodule
